# Fritzing sketch scoreboard (saved by Fritzing 0.7.7b)
breadboards: 1

parts:
  U1 = 74HC595 [package="DIP16 [THT]"]
  U2 = 74HC595 [package="DIP16 [THT]"]
  Arduino1 = Arduino
  7_Segment2 = 7-Segment LED Display [package=THT]
  7_Segment1 = 7-Segment LED Display [package=THT]  # not connected

nets (from the breadboard view):
  GND: U1.GND, U1.OE, U2.GND, U2.OE, Arduino1.GND
  N1: U1.Q7', U2.DS
  VCC: U1.MR, U1.VCC, U2.MR, U2.VCC, Arduino1.+5V, 7_Segment2.commAnode
  N2: U1.SH_CP, U2.SH_CP, Arduino1.D10
  N3: U1.ST_CP, U2.ST_CP, Arduino1.D9
  N4: U1.DS, Arduino1.D8
